// Logisim project Parte dos Lab tablas.circ as structural Verilog
module Union_de_dos_salidas (
  input  A,
  input  B,
  input  C,
  output Z,
  output ZT
);

  and and_1 (Z, A, B);
  and and_2 (ZT, Z, C);
endmodule

module Circuito_con_2_entradas (
  input  A,
  input  B,
  output Z
);

  and and_1 (Z, A, B);
endmodule
